// Logisim project Projeto_Arquitetura-CC3MB.circ as structural Verilog: 16 circuits, main circuit ULA
module ULA (
  input  D,
  input  [3:0] A,
  input  [3:0] B,
  input  [2:0] Operacoes,
  output Overflow,
  output [3:0] S,
  output Zero
);

  wire add_4_1_out_4, and_1_out, and_2_out, decoder_1_s0, decoder_1_s1, decoder_1_s2, decoder_1_s3,
       decoder_1_s4, decoder_1_s5, decoder_1_s6, decoder_1_s7, not_1_out, sub_4_1_out_4;
  wire [3:0] add_4_1_out_5, buffer_5_s, or_4_bits_1_s, rot_d_1_abcd_2, rot_l_1_abcd_2, sub_4_1_out_5;

  or or_1 (Overflow, and_1_out, and_2_out);
  and and_1 (and_1_out, add_4_1_out_4, decoder_1_s1);
  and and_2 (and_2_out, sub_4_1_out_4, decoder_1_s2);
  Decoder decoder_1 (
    .in_1(Operacoes), .S0(decoder_1_s0), .S1(decoder_1_s1), .S2(decoder_1_s2), .S3(decoder_1_s3),
    .S4(decoder_1_s4), .S5(decoder_1_s5), .S6(decoder_1_s6), .S7(decoder_1_s7));
  nor nor_1 (Zero, decoder_1_s7, decoder_1_s6, S[0], S[1], S[2], S[3]);
  Buffer buffer_1 (.B(B), .in_2(decoder_1_s0), .S(S));
  ADD_4 add_4_1 (.in_1(A), .in_2(B), .out_4(add_4_1_out_4), .in_3(1'b0), .out_5(add_4_1_out_5));
  Buffer buffer_2 (.B(add_4_1_out_5), .in_2(decoder_1_s1), .S(S));
  SUB_4 sub_4_1 (.in_1(A), .out_4(sub_4_1_out_4), .in_2(B), .in_3(1'b0), .out_5(sub_4_1_out_5));
  Buffer buffer_3 (.B(sub_4_1_out_5), .in_2(decoder_1_s2), .S(S));
  OR_4_bits or_4_bits_1 (.A(A), .B(B), .S(or_4_bits_1_s));
  Buffer buffer_4 (.B(or_4_bits_1_s), .in_2(decoder_1_s3), .S(S));
  inversor_controlado inversor_controlado_1 (.B(B), .in_2(decoder_1_s4), .S(S));
  ROT_D rot_d_1 (.ABCD(A), .XY(B[1:0]), .abcd_2(rot_d_1_abcd_2));
  ROT_L rot_l_1 (.ABCD(A), .XY(B[1:0]), .abcd_2(rot_l_1_abcd_2));
  not not_1 (not_1_out, D);
  Buffer buffer_5 (.B(rot_d_1_abcd_2), .in_2(D), .S(buffer_5_s));
  Buffer buffer_6 (.B(rot_l_1_abcd_2), .in_2(not_1_out), .S(buffer_5_s));
  Buffer buffer_7 (.B(buffer_5_s), .in_2(decoder_1_s5), .S(S));
endmodule

module ADD_1 (
  input  A,
  input  B,
  input  Vem_C,
  output Soma,
  output Vai
);

  wire A_B_C_2_out, A_B_out, B_C_2_out, B_C_out;

  xor A_B (A_B_out, A, B);
  xor A_B_C (Soma, A_B_out, Vem_C);
  or B_C (B_C_out, B, Vem_C);
  and B_C_2 (B_C_2_out, B, Vem_C);
  and A_B_C_2 (A_B_C_2_out, B_C_out, A);
  or or_1 (Vai, A_B_C_2_out, B_C_2_out);
endmodule

module ADD_4 (
  input  [3:0] in_1,
  input  [3:0] in_2,
  input  in_3,
  output out_4,
  output [3:0] out_5
);

  wire add_1_2_vai, add_1_3_vai, add_1_4_vai;

  ADD_1 add_1_1 (.A(in_1[3]), .B(in_2[3]), .Vem_C(add_1_2_vai), .Soma(out_5[3]), .Vai(out_4));
  ADD_1 add_1_2 (.A(in_1[2]), .B(in_2[2]), .Vem_C(add_1_4_vai), .Soma(out_5[2]), .Vai(add_1_2_vai));
  ADD_1 add_1_3 (.A(in_1[0]), .B(in_2[0]), .Vem_C(in_3), .Soma(out_5[0]), .Vai(add_1_3_vai));
  ADD_1 add_1_4 (.A(in_1[1]), .B(in_2[1]), .Vem_C(add_1_3_vai), .Soma(out_5[1]), .Vai(add_1_4_vai));
endmodule

module SUB_1 (
  input  A,
  input  B,
  input  Vem_C,
  output Subtrai,
  output Vai
);

  wire A_B_C_2_out, A_B_out, B_C_2_out, B_C_out, not_1_out;

  xor A_B (A_B_out, A, B);
  not not_1 (not_1_out, A);
  xor A_B_C (Subtrai, A_B_out, Vem_C);
  or B_C (B_C_out, B, Vem_C);
  and B_C_2 (B_C_2_out, B, Vem_C);
  and A_B_C_2 (A_B_C_2_out, B_C_out, not_1_out);
  or or_1 (Vai, A_B_C_2_out, B_C_2_out);
endmodule

module SUB_4 (
  input  [3:0] in_1,
  input  [3:0] in_2,
  input  in_3,
  output out_4,
  output [3:0] out_5
);

  wire sub_1_2_vai, sub_1_3_vai, sub_1_4_vai;

  SUB_1 sub_1_1 (.A(in_1[3]), .B(in_2[3]), .Vem_C(sub_1_2_vai), .Subtrai(out_5[3]), .Vai(out_4));
  SUB_1 sub_1_2 (.A(in_1[2]), .B(in_2[2]), .Vem_C(sub_1_3_vai), .Subtrai(out_5[2]), .Vai(sub_1_2_vai));
  SUB_1 sub_1_3 (.A(in_1[1]), .B(in_2[1]), .Vem_C(sub_1_4_vai), .Subtrai(out_5[1]), .Vai(sub_1_3_vai));
  SUB_1 sub_1_4 (.A(in_1[0]), .B(in_2[0]), .Vem_C(in_3), .Subtrai(out_5[0]), .Vai(sub_1_4_vai));
endmodule

module Buffer (
  input  [3:0] B,
  input  in_2,
  output [3:0] S
);

  assign S[3] = in_2 ? B[3] : 1'bz;  // Controlled_Buffer controlled_buffer_1
  assign S[2] = in_2 ? B[2] : 1'bz;  // Controlled_Buffer controlled_buffer_2
  assign S[1] = in_2 ? B[1] : 1'bz;  // Controlled_Buffer controlled_buffer_3
  assign S[0] = in_2 ? B[0] : 1'bz;  // Controlled_Buffer controlled_buffer_4
endmodule

module inversor_controlado (
  input  [3:0] B,
  input  in_2,
  output [3:0] S
);

  assign S[3] = in_2 ? ~B[3] : 1'bz;  // Controlled_Inverter controlled_inverter_1
  assign S[2] = in_2 ? ~B[2] : 1'bz;  // Controlled_Inverter controlled_inverter_2
  assign S[1] = in_2 ? ~B[1] : 1'bz;  // Controlled_Inverter controlled_inverter_3
  assign S[0] = in_2 ? ~B[0] : 1'bz;  // Controlled_Inverter controlled_inverter_4
endmodule

module Decoder (
  input  [2:0] in_1,
  output S0,
  output S1,
  output S2,
  output S3,
  output S4,
  output S5,
  output S6,
  output S7
);

  wire not_1_out, not_2_out, not_3_out, not_4_out, not_5_out, not_6_out, not_7_out, not_8_out, not_9_out,
       not_10_out, not_11_out, not_12_out;

  not not_1 (not_1_out, in_1[2]);
  not not_2 (not_2_out, in_1[1]);
  not not_3 (not_3_out, in_1[0]);
  not not_4 (not_4_out, in_1[2]);
  not not_5 (not_5_out, in_1[1]);
  not not_6 (not_6_out, in_1[2]);
  not not_7 (not_7_out, in_1[0]);
  not not_8 (not_8_out, in_1[2]);
  not not_9 (not_9_out, in_1[1]);
  not not_10 (not_10_out, in_1[0]);
  not not_11 (not_11_out, in_1[1]);
  not not_12 (not_12_out, in_1[0]);
  and and_1 (S7, in_1[2], in_1[1], in_1[0]);
  and and_2 (S0, not_1_out, not_2_out, not_3_out);
  and and_3 (S1, not_4_out, not_5_out, in_1[0]);
  and and_4 (S2, not_6_out, in_1[1], not_7_out);
  and and_5 (S3, not_8_out, in_1[1], in_1[0]);
  and and_6 (S4, in_1[2], not_9_out, not_10_out);
  and and_7 (S5, in_1[2], not_11_out, in_1[0]);
  and and_8 (S6, in_1[2], in_1[1], not_12_out);
endmodule

module ROT_L (
  input  [3:0] ABCD,
  input  [1:0] XY,
  output [3:0] abcd_2
);

  wire and_1_out, and_2_out, and_3_out, and_4_out, and_5_out, and_6_out, and_7_out, and_8_out, and_9_out;

  and and_1 (and_1_out, ~XY[1], ~XY[0], ABCD[3]);  // AND_Gate
  and and_2 (and_2_out, ~XY[1], XY[0], ABCD[2]);  // AND_Gate
  and and_3 (and_3_out, XY[1], ~XY[0], ABCD[1]);  // AND_Gate
  and and_4 (and_4_out, XY[1], XY[0], ABCD[0]);
  and and_5 (and_5_out, ~XY[1], ~XY[0], ABCD[2]);  // AND_Gate
  and and_6 (and_6_out, ~XY[1], XY[0], ABCD[1]);  // AND_Gate
  and and_7 (and_7_out, XY[1], ~XY[0], ABCD[0]);  // AND_Gate
  and and_8 (and_8_out, ~XY[1], ~XY[0], ABCD[1]);  // AND_Gate
  and and_9 (and_9_out, ~XY[1], XY[0], ABCD[0]);  // AND_Gate
  and and_10 (abcd_2[0], ~XY[1], ~XY[0], ABCD[0]);  // AND_Gate
  or or_1 (abcd_2[3], and_1_out, and_2_out, and_3_out, and_4_out);
  or or_2 (abcd_2[2], and_5_out, and_6_out, and_7_out);
  or or_3 (abcd_2[1], and_8_out, and_9_out);
endmodule

module ROT_D (
  input  [3:0] ABCD,
  input  [1:0] XY,
  output [3:0] abcd_2
);

  wire and_1_out, and_2_out, and_3_out, and_4_out, and_5_out, and_6_out, and_7_out, and_8_out, and_9_out;

  and and_1 (and_1_out, ~XY[1], ~XY[0], ABCD[0]);  // AND_Gate
  and and_2 (and_2_out, ~XY[1], XY[0], ABCD[1]);  // AND_Gate
  and and_3 (and_3_out, XY[1], ~XY[0], ABCD[2]);  // AND_Gate
  and and_4 (and_4_out, XY[1], XY[0], ABCD[3]);
  and and_5 (and_5_out, ~XY[1], ~XY[0], ABCD[1]);  // AND_Gate
  and and_6 (and_6_out, ~XY[1], XY[0], ABCD[2]);  // AND_Gate
  and and_7 (and_7_out, XY[1], ~XY[0], ABCD[3]);  // AND_Gate
  and and_8 (and_8_out, ~XY[1], ~XY[0], ABCD[2]);  // AND_Gate
  and and_9 (and_9_out, ~XY[1], XY[0], ABCD[3]);  // AND_Gate
  and and_10 (abcd_2[3], ~XY[1], ~XY[0], ABCD[3]);  // AND_Gate
  or or_1 (abcd_2[0], and_1_out, and_2_out, and_3_out, and_4_out);
  or or_2 (abcd_2[1], and_5_out, and_6_out, and_7_out);
  or or_3 (abcd_2[2], and_8_out, and_9_out);
endmodule

module OR_4_bits (
  input  [3:0] B,
  input  [3:0] A,
  output [3:0] S
);

  or or_1 (S[2], A[2], B[2]);
  or or_2 (S[3], A[3], B[3]);
  or or_3 (S[1], A[1], B[1]);
  or or_4 (S[0], A[0], B[0]);
endmodule

module main (
);

  wire Clock_out, not_1_out, not_2_out, Overflow_q, Reset_out, uc_1_clk_ac, uc_1_clk_pc, uc_1_clk_ram,
       uc_1_clk_ri, \uc_1_direção , uc_1_e, uc_1_load, uc_1_r_w, uc_1_rst_pc, ula_1_overflow, ula_1_zero,
       Zero_q;
  wire [2:0] \uc_1_operação ;
  wire [3:0] ac_1_q, counter_1_q, multiplexador_1_s, ram_1_data, uc_1_b__dados, \uc_1_b__endereços ,
       uc_1_operando, ula_1_s;
  wire [7:0] ir_1_q, rom_1_data;

  ROM #(.addrWidth(4)) rom_1 (.addr(counter_1_q), .data(rom_1_data));  // open: sel
  not not_1 (not_1_out, uc_1_load);
  IR ir_1 (.Q(ir_1_q), .D(rom_1_data), .Clock(uc_1_clk_ri));
  Counter #(.width(4), .max('hf), .trigger("falling")) counter_1 (
    .load(uc_1_load), .D(uc_1_b__dados), .count(not_1_out), .Q(counter_1_q), .clk(uc_1_clk_pc),
    .clr(uc_1_rst_pc));  // open: carry
  UC uc_1 (
    .Operando(uc_1_operando), .\Direção (\uc_1_direção ), .E(uc_1_e), .\Operação (\uc_1_operação ),
    .\Instrução (ir_1_q), .\B__Endereços (\uc_1_b__endereços ), .clk_RI(uc_1_clk_ri), .clk_PC(uc_1_clk_pc),
    .clk_AC(uc_1_clk_ac), .clk_RAM(uc_1_clk_ram), .RESET(Reset_out), .CLOCK(Clock_out), .rst_PC(uc_1_rst_pc),
    .B__Dados(uc_1_b__dados), .OverFlow(Overflow_q), .Zero(Zero_q), .R_W(uc_1_r_w), .Load(uc_1_load));
  Clock Clock (.out(Clock_out));
  Button Reset (.out(Reset_out));
  // Probe on ac_1_q
  Multiplexador multiplexador_1 (.E(uc_1_operando), .Controle(uc_1_e), .D(ram_1_data), .S(multiplexador_1_s));
  // Probe on multiplexador_1_s
  ULA ula_1 (
    .D(\uc_1_direção ), .A(ac_1_q), .B(multiplexador_1_s), .Operacoes(\uc_1_operação ), .S(ula_1_s),
    .Overflow(ula_1_overflow), .Zero(ula_1_zero));
  // Probe on ula_1_s
  AC ac_1 (.Q(ac_1_q), .D(ula_1_s), .Clock(uc_1_clk_ac));
  D_Flip_Flop Overflow (.clk(uc_1_clk_ac), .D(ula_1_overflow), .Q(Overflow_q));  // open: Qn, preset, en, reset
  D_Flip_Flop Zero (.clk(uc_1_clk_ac), .D(ula_1_zero), .Q(Zero_q));  // open: Qn, preset, en, reset
  RAM #(.addrWidth(4), .dataWidth(4)) ram_1 (
    .addr(\uc_1_b__endereços ), .data(ram_1_data), .clk(uc_1_clk_ram), .ld(uc_1_r_w));  // open: sel, clr
  not not_2 (not_2_out, uc_1_r_w);
  Buffer buffer_1 (.B(ac_1_q), .in_2(not_2_out), .S(ram_1_data));

  // Notes on the sheet:
  //   MOV
  //   0
  //   1
  //   MOV
  //   2
  //   ADD
  //   3
  //   ADD
  //   SUB
  //   4
  //   5
  //   SUB
  //   6
  //   OR
  //   OR
  //   7
  //   NOT
  //   8
  //   NOT
  //   9
  //   SHF
  //   A
  //   B
  //   SHF
  //   C
  //   JPZ
  //   JPO
  //   D
  //   GO
  //   E
  //   STR
  //   F
  //   Instruction Set
  //   0
  //   000
  //   AC <= X
  //   1
  //   000
  //   0
  //   001
  //   1
  //   001
  //   0
  //   010
  //   1
  //   010
  //   0
  //   011
  //   1
  //   011
  //   0
  //   100
  //   100
  //   1
  //   101
  //   0
  //   1
  //   101
  //   110
  //   0
  //   1
  //   110
  //   PC <= X
  //   0
  //   111
  //   1
  //   111
  //   AC <= M(X)
  //   AC <= AC+X
  //   AC <= AC+M(X)
  //   AC <= AC-X
  //   AC <= AC-M(X)
  //   AC <= AC OR X
  //   AC <= AC OR M(X)
  //   AC <= NOT X
  //   AC <= NOT M( X)
  //   AC <= AC << Q
  //   AC <= AC >> Q
  //   PC <= X SE FLAG Z
  //   PC <= X SE FLAG O
  //   M(X) <= AC 
  //   Progam Memory
  //   contents of rom_1 (hex, n*v repeats v):
  //   0 f0 1 f1 10 31 d0 f2 11 f0 12 f1 e4
  //   Data Memory
endmodule

module AC (
  input  Clock,
  input  [3:0] D,
  output [3:0] Q
);

  D_Flip_Flop D3 (.clk(Clock), .D(D[3]), .Q(Q[3]));  // open: Qn, preset, en, reset
  D_Flip_Flop D2 (.clk(Clock), .D(D[2]), .Q(Q[2]));  // open: Qn, preset, en, reset
  D_Flip_Flop D1 (.clk(Clock), .D(D[1]), .Q(Q[1]));  // open: Qn, preset, en, reset
  D_Flip_Flop D0 (.clk(Clock), .D(D[0]), .Q(Q[0]));  // open: Qn, preset, en, reset
endmodule

module Multiplexador (
  input  [3:0] E,
  input  [3:0] D,
  input  Controle,
  output [3:0] S
);

  wire not_1_out;

  not not_1 (not_1_out, Controle);
  Buffer buffer_1 (.B(E), .in_2(not_1_out), .S(S));
  Buffer buffer_2 (.B(D), .in_2(Controle), .S(S));
endmodule

module IR (
  input  Clock,
  input  [7:0] D,
  output [7:0] Q
);

  D_Flip_Flop #(.trigger("falling")) D3 (.clk(Clock), .D(D[7]), .Q(Q[7]));  // open: Qn, preset, en, reset
  D_Flip_Flop #(.trigger("falling")) D2 (.clk(Clock), .D(D[6]), .Q(Q[6]));  // open: Qn, preset, en, reset
  D_Flip_Flop #(.trigger("falling")) D1 (.clk(Clock), .D(D[5]), .Q(Q[5]));  // open: Qn, preset, en, reset
  D_Flip_Flop #(.trigger("falling")) D0 (.clk(Clock), .D(D[4]), .Q(Q[4]));  // open: Qn, preset, en, reset
  D_Flip_Flop #(.trigger("falling")) D3_2 (.clk(Clock), .D(D[3]), .Q(Q[3]));  // open: Qn, preset, en, reset
  D_Flip_Flop #(.trigger("falling")) D2_2 (.clk(Clock), .D(D[2]), .Q(Q[2]));  // open: Qn, preset, en, reset
  D_Flip_Flop #(.trigger("falling")) D1_2 (.clk(Clock), .D(D[1]), .Q(Q[1]));  // open: Qn, preset, en, reset
  D_Flip_Flop #(.trigger("falling")) D0_2 (.clk(Clock), .D(D[0]), .Q(Q[0]));  // open: Qn, preset, en, reset
endmodule

module UC (
  input  CLOCK,
  input  [7:0] \Instrução ,
  input  RESET,
  input  Zero,
  input  OverFlow,
  output clk_RI,
  output clk_AC,
  output [3:0] B__Dados,
  output clk_RAM,
  output [3:0] \B__Endereços ,
  output [3:0] Operando,
  output rst_PC,
  output clk_PC,
  output \Direção ,
  output E,
  output [2:0] \Operação ,
  output R_W,
  output Load
);

  wire GoTo_out, JPO_out, JPZ_out, nand_1_out;
  wire [1:0] counter_1_q;

  Counter #(.width(2), .max('h3)) counter_1 (.Q(counter_1_q), .clk(CLOCK), .clr(RESET));  // open: load, D, count, carry
  and GoTo (GoTo_out, \Instrução [7], \Instrução [6], \Instrução [5], ~\Instrução [4], clk_PC);  // AND_Gate
  nand Storage (R_W, \Instrução [7], \Instrução [6], \Instrução [5], \Instrução [4], clk_AC);
  and JPO (JPO_out, \Instrução [7], \Instrução [6], ~\Instrução [5], \Instrução [4], clk_PC, OverFlow);  // AND_Gate
  or or_1 (Load, GoTo_out, JPO_out, JPZ_out);
  and and_1 (clk_PC, counter_1_q[0], ~counter_1_q[1]);  // AND_Gate
  and and_2 (clk_RI, ~counter_1_q[0], ~counter_1_q[1]);  // AND_Gate
  and and_3 (clk_AC, ~counter_1_q[0], counter_1_q[1]);  // AND_Gate
  and and_4 (clk_RAM, counter_1_q[0], counter_1_q[1]);
  and JPZ (JPZ_out, \Instrução [7], \Instrução [6], ~\Instrução [5], ~\Instrução [4], clk_PC, Zero);  // AND_Gate
  nand nand_1 (nand_1_out, \Instrução [7], ~\Instrução [6], \Instrução [5]);  // NAND_Gate
  and and_5 (E, \Instrução [4], nand_1_out);

  assign B__Dados = \Instrução [3:0];
  assign \B__Endereços  = \Instrução [3:0];
  assign \Direção  = \Instrução [4];
  assign Operando = \Instrução [3:0];
  assign \Operação  = \Instrução [7:5];
  assign rst_PC = RESET;
endmodule
